# Fritzing sketch schematic (saved by Fritzing 0.9.3b)
breadboards: 1

parts:
  Part1 = Arduino Nano (Rev3.0)
  Shift_register_LOW = 74HC595 [package="DIP16 [THT]"]
  Shift_register_HIGH = 74HC595 [package="DIP16 [THT]"]
  J2 = female pin header, 14 pins [form="♀ (female)"]
  J1 = female pin header, 14 pins [form="♀ (female)"]

nets:
  GND: Part1.GND, Shift_register_LOW.GND, Shift_register_LOW.OE, Shift_register_HIGH.GND, Shift_register_HIGH.OE, J2.pin14
  N1: Part1.D2, J2.pin13
  N2: Part1.D3, J1.pin1
  N3: Part1.D4, J1.pin2
  N4: Part1.D5, J1.pin3
  N5: Part1.D6, J1.pin4
  N6: Part1.D7, J1.pin5
  N7: Part1.D8, J1.pin13
  N8: Part1.D9, J1.pin8
  N9: Part1.D10, Shift_register_LOW.DS
  N10: Part1.D11/MOSI, Shift_register_LOW.ST_CP, Shift_register_HIGH.ST_CP
  VCC: Part1.5V, Shift_register_LOW.MR, Shift_register_LOW.VCC, Shift_register_HIGH.MR, Shift_register_HIGH.VCC, J1.pin6, J1.pin14
  N11: Part1.A4, J2.pin12
  N12: Part1.A3, J2.pin11
  N13: Part1.D13/SCK, Shift_register_LOW.SH_CP, Shift_register_HIGH.SH_CP
  N14: Shift_register_LOW.Q1, J2.pin9
  N15: Shift_register_LOW.Q2, J2.pin8
  N16: Shift_register_LOW.Q3, J2.pin7
  N17: Shift_register_LOW.Q4, J2.pin6
  N18: Shift_register_LOW.Q5, J2.pin5
  N19: Shift_register_LOW.Q6, J2.pin4
  N20: Shift_register_LOW.Q7, J2.pin3
  N21: Shift_register_LOW.Q7', Shift_register_HIGH.DS
  N22: Shift_register_LOW.Q0, J2.pin10
  N23: Shift_register_HIGH.Q1, J1.pin10
  N24: Shift_register_HIGH.Q2, J1.pin7
  N25: Shift_register_HIGH.Q3, J1.pin9
  N26: Shift_register_HIGH.Q4, J2.pin2
  N27: Shift_register_HIGH.Q5, J1.pin12
  N28: Shift_register_HIGH.Q6, J2.pin1
  N29: Shift_register_HIGH.Q0, J1.pin11

notes:
  EEPROM goes here
